# Fritzing sketch sensor_presenca_esquema (saved by Fritzing 0.9.1b)
breadboards: 1

parts:
  Componente1 = Arduino Uno (Rev3)
  U2 = Adafruit PIR [part_number=189 package=THT]
  U3 = Adafruit PIR [part_number=189 package=THT]
  U4 = Adafruit PIR [part_number=189 package=THT]
  U5 = Adafruit PIR [part_number=189 package=THT]

nets:
  N1: Componente1.D2, U3.pin2
  N2: Componente1.D3_PWM, U2.pin2
  N3: Componente1.D4, U4.pin2
  N4: Componente1.D5_PWM, U5.pin2
  N5: Componente1.5V, U2.pin3, U3.pin3, U4.pin3, U5.pin3
  N6: Componente1.GND, U2.pin1, U3.pin1, U4.pin1, U5.pin1

notes:
  SENSOR PIR (PRESENÇA)
  PROJETO COM 4 SENSORES
  Vermelho = VDD 5v
  Amarelo = Sinal
  Preto = GND
  Resistencia = 10k

custom parts:
  Adafruit PIR: Size: Rectangular Price: $10.00 at the Adafruit shop Output: Digital pulse high (3V) when triggered (motion detected) digital low when idle (no motion detected). Pulse lengths are determined by resistors and capacitors on the PCB and differ from sensor to sensor. Sensitivity range: up to 20 feet (6 meters) 110° x 70° detection range Power supply: 5V-9V input voltage, BIS0001 Datasheet (the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

// code stored in the sketch: sensor_presenca.ino
//importando bibliotecas
#include <stdint.h>
#include <util/delay.h>

#define pir 2 //entrada para o sensor de movimento

void readSensor(); //função auxiliar para ler o sensor

unsigned long sensorIn = 0; //variavel para armazenar a duração do pulso


void setup() {
  Serial.begin(300); //frequencia da porta serial. Define a taxa de dados em bits por segundo para transmissão de dados serial.
  pinMode(pir, INPUT); //defini o sensor de presença como entrada
}

void loop() {
  readSensor(); //lê o sensor

  if(sensorIn >1E6 && sensorIn <4E6){ //testa se a largura do pulso é maior que 1 e menos que 4 segundos
    Serial.print(1); //envia para a porta serial o valor 1
  }else{
    Serial.print(0); //envia para a porta serial o valor 0 caso não aja presença
  }
}


void readSensor(){
  sensorIn = pulseIn(pir, HIGH); //Lê a duração do pulso do sensor em pulso auto e armazena nessa variavel. pulseIn lê a largura de um pulso em uma entrada digital
  delay(5000); //intervalo entre as leituras
}
